# Fritzing sketch fuse_schematic (saved by Fritzing 0.9.3b)

parts:
  Part1 = Arduino Nano (Rev3.0)
  Part2 = IFR520 MOS module [package=THT]
  Part3 = Bluetooth HC-05 Macho
  BAT1 = BC9VPC [package=bc9vpc]
  L1 = Inductor [package="1206 [SMD]"]

nets:
  GND: Part1.GND, Part2.GND, BAT1.V-
  N1: Part1.D6, Part3.RXD
  N2: Part1.D7, Part3.TXD
  N3: Part1.D10, Part2.SIG
  5V: Part1.5V, Part2.VCC
  N4: Part2.V+, L1.pin_0
  N5: Part2.V-, L1.pin_1
  N6: Part2.VIN, BAT1.V+

// code stored in the sketch: fuse_program.ino
// Fuse program by naveenraj

#include <SoftwareSerial.h>

SoftwareSerial BTSerial(7, 6); // RX | TX

String readString;

const int fusepin = 5;


void setup()
{
  BTSerial.begin(115200);
  BTSerial.println("Electric fuse ready");
  pinMode(fusepin, OUTPUT);
  digitalWrite(fusepin, HIGH);
}

void loop()
{
  while (BTSerial.available() > 0)
  {
    char cmd = BTSerial.read();
    Serial.println(cmd);

    switch(cmd)
    {
      case 'F':
          fuse_on();
          break;
      case 'S':
          fuse_off();
          break;
    }
  }
}

void fuse_on()
{
  digitalWrite(fusepin, LOW);
  //BTSerial.write("fuse on\n");
}

void fuse_off()
{
  digitalWrite(fusepin, HIGH);
  //BTSerial.write("fuse off\n");
}
